# Fritzing sketch LED Blink Schematic (saved by Fritzing 0.9.3b)
breadboards: 1

parts:
  Part1 = Arduino Nano (Rev3.0)
  LED1 = smd LED [color="Red (633nm)" package="1206 [SMD]"]
  LED2 = smd LED [color="Red (633nm)" package="1206 [SMD]"]
  R1 = Rotary Potentiometer (Small) [maximum_resistance=100kΩ package=THT]
  R2 = Resistor [tolerance=±5% resistance=220 package="1206 [SMD]"]
  S1 = Round Pushbutton

nets:
  N1: Part1.GND, Part1.D3, Part1.D5, Part1.D6, LED1.cathode, LED1.anode, LED2.cathode, LED2.anode, R1.leg1, R2.Pin_0, S1.leg0, S1.leg1
  N2: Part1.5V, R1.leg2, R2.Pin_1
  N3: Part1.A0, R1.wiper
